// Logisim project mac.circ as structural Verilog
module main_2 (
);

  wire clk, comparator_2_lt, comparator_4_eq, comparator_5_eq, counter_1_q, counter_2_q, is_l0, latch_op,
       m0_l, m0_rst, m1_l, m1_rst, m2_l, m2_rst, m3_l, m3_rst, m4_l, m4_rst, m5_l, m5_rst, m6_l, m6_rst,
       m7_l, m7_rst, m8_l, m8_rst, m9_l, m9_rst, m10_l, m10_rst, m11_l, m11_rst, m12_l, m12_rst, m13_l,
       m13_rst, m14_l, m14_rst, m15_l, m15_rst, multiplexer_14_out, not_1_out, rst, rst_l3, sel_bias,
       undriven;
  wire [1:0] layer;
  wire [2:0] counter_9_q, rst_switch_sw3;
  wire [3:0] plex_index;
  wire [4:0] rgb_video_1_p4, rgb_video_1_p5;
  wire [5:0] counter_7_q;
  wire [7:0] m0_b, m1_b, m2_b, m3_b, m4_b, m5_b, m6_b, m7_b, m8_b, m9_b, m10_b, m11_b, m12_b, m13_b, m14_b,
       m15_b, op0, op1, op2, op3, op4, op5, op6, op7, op8, op9, op10, op11, op12, op13, op14, op15,
       register_1_q, rom_img_data;
  wire [9:0] control_rom1_data, counter_6_q, counter_8_q, curr_iter;
  wire [15:0] multiplexer_10_out;
  wire [63:0] b_rom0_opt0, b_rom0_opt1, inp0, inp1, m0_w0, m0_w1, m0_x0, m0_x1, m1_w0, m1_w1, m1_x0, m1_x1,
       m2_w0, m2_w1, m2_x0, m2_x1, m3_w0, m3_w1, m3_x0, m3_x1, m4_w0, m4_w1, m4_wo, m4_x0, m4_x1, m5_w0,
       m5_w1, m5_x0, m5_x1, m6_w0, m6_w1, m6_x0, m6_x1, m7_w0, m7_w1, m7_x0, m7_x1, m8_w0, m8_w1, m8_x0,
       m8_x1, m9_w0, m9_w1, m9_x0, m9_x1, m10_w0, m10_w1, m10_x0, m10_x1, m11_w0, m11_w1, m11_x0, m11_x1,
       m12_w0, m12_w1, m12_x0, m12_x1, m13_w0, m13_w1, m13_x0, m13_x1, m14_w0, m14_w1, m14_x0, m14_x1,
       m15_w0, m15_w1, m15_x0, m15_x1, multiplexer_3_out, multiplexer_4_out, w_0, w_1, w_rom00_opt0,
       w_rom01_opt1;

  // Probe on m0_x0
  // Probe on op0
  Register register_1 (.Q(register_1_q));  // open: D, en, clk, clr
  // Probe on m0_w0
  // Probe on op1
  // Probe on op4
  // Probe on op2
  // Probe on op5
  // Probe on op6
  Comparator #(.mode("unsigned"), .width(2)) comparator_1 (.a(layer), .b(2'b00), .eq(is_l0));  // open: gt, lt
  ROM #(.dataWidth(10)) control_rom1 (.addr(register_1_q), .data(control_rom1_data));
  ROM #(.addrWidth(16)) meta_data_rom1 ();  // open: addr, data
  Counter #(.max('h1), .width(1)) counter_1 (
    .load(undriven), .Q(counter_1_q), .clk(clk), .clr(rst));  // open: D, count, carry, up
  // Probe on op3
  // Probe on op7
  Multiplexer #(.width(64)) multiplexer_1 (.in0(w_rom00_opt0), .in1(w_rom00_opt0), .out(w_0), .sel(counter_1_q));
  Multiplexer #(.width(64)) multiplexer_2 (.in0(w_rom01_opt1), .in1(w_rom01_opt1), .out(w_1), .sel(counter_1_q));
  mac_p m0 (
    .w0(m0_w0), .x0(m0_x0), .w1(m0_w1), .x1(m0_x1), .b(m0_b), .latch_op(latch_op), .latch_ip(m0_l),
    .rst(m0_rst), .opt(op0));
  mac_p m4 (
    .w0(m4_w0), .x0(m4_x0), .w1(m4_w1), .x1(m4_x1), .b(m4_b), .latch_op(latch_op), .latch_ip(m4_l),
    .rst(m4_rst), .opt(op4));
  mac_p m8 (
    .w0(m8_w0), .x0(m8_x0), .w1(m8_w1), .x1(m8_x1), .b(m8_b), .latch_op(latch_op), .latch_ip(m8_l),
    .rst(m8_rst), .opt(op8));
  mac_p m12 (
    .w0(m12_w0), .x0(m12_x0), .w1(m12_w1), .x1(m12_x1), .b(m12_b), .latch_op(latch_op), .latch_ip(m12_l),
    .rst(m12_rst), .opt(op12));
  // Probe on m1_x0
  // Probe on {op7, op6, op5, op4, op3, op2, op1, op0}
  Multiplexer #(.width(64)) multiplexer_3 (
    .in0({op7, op6, op5, op4, op3, op2, op1, op0}), .in1(inp0), .out(multiplexer_3_out), .sel(is_l0));
  // Probe on m1_w0
  Demultiplexer #(.select(4), .width(64)) demultiplexer_1 (
    .out0(m0_x0), .out1(m1_x0), .out2(m2_x0), .out3(m3_x0), .out4(m4_x0), .out5(m5_x0), .out6(m6_x0),
    .out7(m7_x0), .out8(m8_x0), .out9(m9_x0), .out10(m10_x0), .out11(m11_x0), .out12(m12_x0), .out13(m13_x0),
    .out14(m14_x0), .out15(m15_x0), .in(multiplexer_3_out), .sel(plex_index));
  mac_p m1 (
    .w0(m1_w0), .x0(m1_x0), .w1(m1_w1), .x1(m1_x1), .b(m1_b), .latch_op(latch_op), .latch_ip(m1_l),
    .rst(m1_rst), .opt(op1));
  mac_p m5 (
    .w0(m5_w0), .x0(m5_x0), .w1(m5_w1), .x1(m5_x1), .b(m5_b), .latch_op(latch_op), .latch_ip(m5_l),
    .rst(m5_rst), .opt(op5));
  mac_p m9 (
    .w0(m9_w0), .x0(m9_x0), .w1(m9_w1), .x1(m9_x1), .b(m9_b), .latch_op(latch_op), .latch_ip(m9_l),
    .rst(m9_rst), .opt(op9));
  mac_p m13 (
    .w0(m13_w0), .x0(m13_x0), .w1(m13_w1), .x1(m13_x1), .b(m13_b), .latch_op(latch_op), .latch_ip(m13_l),
    .rst(m13_rst), .opt(op13));
  // Probe on m2_x0
  // Probe on m2_w0
  // Probe on plex_index
  // Probe on {op15, op14, op13, op12, op11, op10, op9, op8}
  Multiplexer #(.width(64)) multiplexer_4 (
    .in0({op15, op14, op13, op12, op11, op10, op9, op8}), .in1(inp1), .out(multiplexer_4_out), .sel(is_l0));
  Demultiplexer #(.select(4), .width(64)) demultiplexer_2 (
    .out0(m0_x1), .out1(m1_x1), .out2(m2_x1), .out3(m3_x1), .out4(m4_x1), .out5(m5_x1), .out6(m6_x1),
    .out7(m7_x1), .out8(m8_x1), .out9(m9_x1), .out10(m10_x1), .out11(m11_x1), .out12(m12_x1), .out13(m13_x1),
    .out14(m14_x1), .out15(m15_x1), .in(multiplexer_4_out), .sel(plex_index));
  Demultiplexer #(.select(4)) demultiplexer_3 (
    .out0(m0_l), .out1(m1_l), .out2(m2_l), .out3(m3_l), .out4(m4_l), .out5(m5_l), .out6(m6_l), .out7(m7_l),
    .out8(m8_l), .out9(m9_l), .out10(m10_l), .out11(m11_l), .out12(m12_l), .out13(m13_l), .out14(m14_l),
    .out15(m15_l), .in(1'b1), .sel(plex_index));
  mac_p m2 (
    .w0(m2_w0), .x0(m2_x0), .w1(m2_w1), .x1(m2_x1), .b(m2_b), .latch_op(latch_op), .latch_ip(m2_l),
    .rst(m2_rst), .opt(op2));
  mac_p m6 (
    .w0(m6_w0), .x0(m6_x0), .w1(m6_w1), .x1(m6_x1), .b(m6_b), .latch_op(latch_op), .latch_ip(m6_l),
    .rst(m6_rst), .opt(op6));
  mac_p m10 (
    .w0(m10_w0), .x0(m10_x0), .w1(m10_w1), .x1(m10_x1), .b(m10_b), .latch_op(latch_op), .latch_ip(m10_l),
    .rst(m10_rst), .opt(op10));
  mac_p m14 (
    .w0(m14_w0), .x0(m14_x0), .w1(m14_w1), .x1(m14_x1), .b(m14_b), .latch_op(latch_op), .latch_ip(m14_l),
    .rst(m14_rst), .opt(op14));
  Demultiplexer #(.select(4), .width(64)) demultiplexer_4 (
    .out0(m0_w0), .out1(m1_w0), .out2(m2_w0), .out3(m3_w0), .out4(m4_wo), .out5(m5_w0), .out6(m6_w0),
    .out7(m7_w0), .out8(m8_w0), .out9(m9_w0), .out10(m10_w0), .out11(m11_w0), .out12(m12_w0), .out13(m13_w0),
    .out14(m14_w0), .out15(m15_w0), .in(w_0), .sel(plex_index));
  // Probe on m3_x0
  // Probe on m3_w0
  // Probe on op12
  // Probe on op8
  // Probe on plex_index
  // Probe on op13
  // Probe on op9
  // Probe on op10
  Demultiplexer #(.select(4), .width(64)) demultiplexer_5 (
    .out0(m0_w1), .out1(m1_w1), .out2(m2_w1), .out3(m3_w1), .out4(m4_w1), .out5(m5_w1), .out6(m6_w1),
    .out7(m7_w1), .out8(m8_w1), .out9(m9_w1), .out10(m10_w1), .out11(m11_w1), .out12(m12_w1), .out13(m13_w1),
    .out14(m14_w1), .out15(m15_w1), .in(w_1), .sel(plex_index));
  // Probe on op14
  // Probe on op15
  // Probe on op11
  mac_p m3 (
    .w0(m3_w0), .x0(m3_x0), .w1(m3_w1), .x1(m3_x1), .b(m3_b), .latch_op(latch_op), .latch_ip(m3_l),
    .rst(m3_rst), .opt(op3));
  mac_p m7 (
    .w0(m7_w0), .x0(m7_x0), .w1(m7_w1), .x1(m7_x1), .b(m7_b), .latch_op(latch_op), .latch_ip(m7_l),
    .rst(m7_rst), .opt(op7));
  mac_p m11 (
    .w0(m11_w0), .x0(m11_x0), .w1(m11_w1), .x1(m11_x1), .b(m11_b), .latch_op(latch_op), .latch_ip(m11_l),
    .rst(m11_rst), .opt(op11));
  mac_p m15 (
    .w0(m15_w0), .x0(m15_x0), .w1(m15_w1), .x1(m15_x1), .b(m15_b), .latch_op(latch_op), .latch_ip(m15_l),
    .rst(m15_rst), .opt(op15));
  Multiplexer #(.width(8)) multiplexer_5 (.in0(op0), .in1(b_rom0_opt0[7:0]), .out(m0_b), .sel(sel_bias));
  Multiplexer #(.width(8)) multiplexer_6 (.in0(op1), .in1(b_rom0_opt0[15:8]), .out(m1_b), .sel(sel_bias));
  Multiplexer #(.width(8)) multiplexer_7 (.in0(op2), .in1(b_rom0_opt0[23:16]), .out(m2_b), .sel(sel_bias));
  Multiplexer #(.width(8)) multiplexer_8 (.in0(op8), .in1(b_rom0_opt1[7:0]), .out(m8_b), .sel(sel_bias));
  Multiplexer #(.width(8)) multiplexer_9 (.in0(op9), .in1(b_rom0_opt1[15:8]), .out(m9_b), .sel(sel_bias));
  Comparator #(.mode("unsigned"), .width(10)) comparator_2 (
    .a(curr_iter), .b(10'h10), .lt(comparator_2_lt));  // open: gt, eq
  Multiplexer #(.select(3), .width(16)) multiplexer_10 (
    .in0({16{1'b0}}), .in1({16{1'b1}}), .in2(16'hf000), .out(multiplexer_10_out), .sel(rst_switch_sw3));  // open: in3, in4, in5, in6, in7
  DipSwitch #(.number(3)) rst_switch (.sw1(rst_switch_sw3[2]), .sw2(rst_switch_sw3[1]), .sw3(rst_switch_sw3[0]));
  Counter #(.max('h1), .width(1)) counter_2 (
    .Q(counter_2_q), .clk(comparator_4_eq), .clr(rst));  // open: load, D, count, carry, up
  Multiplexer #(.width(8)) multiplexer_11 (.in0(op3), .in1(b_rom0_opt0[31:24]), .out(m3_b), .sel(sel_bias));
  Multiplexer #(.width(8)) multiplexer_12 (.in0(op10), .in1(b_rom0_opt1[23:16]), .out(m10_b), .sel(sel_bias));
  Multiplexer #(.width(8)) multiplexer_13 (.in0(op11), .in1(b_rom0_opt1[31:24]), .out(m11_b), .sel(sel_bias));
  and and_1 (sel_bias, is_l0, comparator_2_lt);
  Clock clock_1 (.out(clk));
  Button u_rst (.out(rst));
  Register #(.width(16)) register_2 (
    .D(multiplexer_10_out), .en(1'b1),
    .Q({m12_rst, m13_rst, m14_rst, m15_rst, m8_rst, m9_rst, m10_rst, m11_rst, m4_rst, m5_rst, m6_rst, m7_rst, m0_rst, m1_rst, m2_rst, m3_rst}),
    .clk(clk), .clr(rst));
  Button u_rst_l3 (.out(rst_l3));
  Counter #(.max('h3), .width(2)) counter_3 (
    .Q(layer), .clk(multiplexer_14_out), .clr(rst));  // open: load, D, count, carry, up
  Multiplexer multiplexer_14 (.in0(latch_op), .in1(comparator_4_eq), .out(multiplexer_14_out), .sel(not_1_out));
  not not_1 (not_1_out, counter_2_q);
  Counter #(.max('h3ff), .width(10)) counter_4 (
    .Q(curr_iter), .clk(clk), .clr(rst));  // open: load, D, count, carry, up
  Counter #(.max('hf), .width(4)) counter_5 (.Q(plex_index), .clk(clk), .clr(rst));  // open: load, D, count, carry, up
  ROM #(.addrWidth(10)) rom_img (.addr(counter_6_q), .data(rom_img_data));
  Comparator #(.mode("unsigned"), .width(4)) comparator_3 (.a(plex_index), .b(4'b1111), .eq(latch_op));  // open: gt, lt
  // Probe on layer
  Comparator #(.mode("unsigned"), .width(10)) comparator_4 (
    .a(curr_iter), .b({10{1'b1}}), .eq(comparator_4_eq));  // open: gt, lt
  Counter #(.max('h3ff), .width(10)) counter_6 (
    .Q(counter_6_q), .clk(clk), .clr(rst));  // open: load, D, count, carry, up
  Multiplexer #(.width(8)) multiplexer_15 (.in0(op4), .in1(b_rom0_opt0[39:32]), .out(m4_b), .sel(sel_bias));
  Multiplexer #(.width(8)) multiplexer_16 (.in0(op5), .in1(b_rom0_opt0[47:40]), .out(m5_b), .sel(sel_bias));
  Multiplexer #(.width(8)) multiplexer_17 (.in0(op12), .in1(b_rom0_opt1[39:32]), .out(m12_b), .sel(sel_bias));
  Multiplexer #(.width(8)) multiplexer_18 (.in0(op6), .in1(b_rom0_opt0[55:48]), .out(m6_b), .sel(sel_bias));
  Multiplexer #(.width(8)) multiplexer_19 (.in0(op7), .in1(b_rom0_opt0[63:56]), .out(m7_b), .sel(sel_bias));
  Multiplexer #(.width(8)) multiplexer_20 (.in0(op13), .in1(b_rom0_opt1[47:40]), .out(m13_b), .sel(sel_bias));
  Multiplexer #(.width(8)) multiplexer_21 (.in0(op14), .in1(b_rom0_opt1[55:48]), .out(m14_b), .sel(sel_bias));
  Multiplexer #(.width(8)) multiplexer_22 (.in0(op15), .in1(b_rom0_opt1[63:56]), .out(m15_b), .sel(sel_bias));
  control_unit CONTROL_UNIT_INSTANCE ();
  // RGB_Video #(.height(32), .scale(8), .width(32)) rgb_video_1: pin names not known; wires that end beside it: rst, clk, 1'b1, rgb_video_1_p4, rgb_video_1_p5, {{16{1'b0}}, rom_img_data}
  Counter #(.max('h1f), .width(5)) x_cdnt (
    .Q(rgb_video_1_p4), .clk(clk), .clr(rst));  // open: load, D, count, carry, up
  Counter #(.max('h1f), .width(5)) y_cdnt (
    .Q(rgb_video_1_p5), .clk(comparator_5_eq), .clr(rst));  // open: load, D, count, carry, up
  Comparator #(.width(5)) comparator_5 (.a(rgb_video_1_p4), .b({5{1'b1}}), .eq(comparator_5_eq));  // open: gt, lt
  Counter #(.max('h3f), .width(6)) counter_7 (
    .Q(counter_7_q), .clk(clk), .clr(rst));  // open: load, D, count, carry, up
  Counter #(.max('h3ff), .width(10)) counter_8 (
    .Q(counter_8_q), .clk(clk), .clr(rst));  // open: load, D, count, carry, up
  Counter #(.max('h7), .width(3)) counter_9 (.Q(counter_9_q), .clk(clk), .clr(rst));  // open: load, D, count, carry, up
  ROM #(.addrWidth(6), .dataWidth(64)) input_rom0 (.addr(counter_7_q), .data(inp0));
  ROM #(.addrWidth(10), .dataWidth(64)) w_rom00 (.addr(counter_8_q), .data(w_rom00_opt0));
  ROM #(.addrWidth(3), .dataWidth(64)) b_rom00 (.addr(counter_9_q), .data(b_rom0_opt0));
  ROM #(.addrWidth(6), .dataWidth(64)) input_rom1 (.addr(counter_7_q), .data(inp1));
  ROM #(.addrWidth(10), .dataWidth(64)) w_rom01 (.addr(counter_8_q), .data(w_rom01_opt1));
  ROM #(.addrWidth(3), .dataWidth(64)) b_rom01 (.addr(counter_9_q), .data(b_rom0_opt1));

  // Other names for the same wires on the sheet: layer_done = latch_op;
  //   rst_all[15:0] = {m12_rst, m13_rst, m14_rst, m15_rst, m8_rst, m9_rst, m10_rst, m11_rst, m4_rst, m5_rst, m6_rst, m7_rst, m0_rst, m1_rst, m2_rst, m3_rst}

  // Notes on the sheet:
  //   contents of control_rom1 (hex, n*v repeats v):
  //   1 1
  //   contents of meta_data_rom1 (hex, n*v repeats v):
  //   1
  //   contents of rom_img (hex, n*v repeats v):
  //   230*0 54 b9 9f 97 3c 24 26*0 de 4*fe f1 8*c6 aa 34 16*0 43 72 48 72 a3 e3 fe e1 fe fe fe fa e5 fe fe
  //   8c 21*0 11 42 e 43 43 43 3b 15 ec fe 6a 28*0 53 fd d1 12 27*0 16 e9 ff 53 28*0 81 fe ee 2c 27*0 3b
  //   f9 fe 3e 28*0 85 fe bb 5 27*0 9 cd f8 3a 28*0 7e fe b6 28*0 4b fb f0 39 27*0 13 dd fe a6 27*0 3 cb
  //   fe db 23 27*0 26 fe fe 4d 27*0 1f e0 fe 73 1 27*0 85 fe fe 34 27*0 3d f2 fe fe 34 27*0 79 fe fe db
  //   28 27*0 79 fe cf 12
  //   contents of input_rom0 (hex, n*v repeats v):
  //   16*1
  //   contents of w_rom00 (hex, n*v repeats v):
  //   16*1
  //   contents of b_rom00 (hex, n*v repeats v):
  //   1
  //   contents of input_rom1 (hex, n*v repeats v):
  //   24*1
  //   contents of w_rom01 (hex, n*v repeats v):
  //   16*1
  //   contents of b_rom01 (hex, n*v repeats v):
  //   1
endmodule

module mac_p (
  input  [63:0] w0,
  input  [63:0] x0,
  input  [63:0] w1,
  input  [63:0] x1,
  input  [7:0] b,
  input  latch_op,
  input  latch_ip,
  input  rst,
  output [7:0] opt
);

  wire ad0, ad1, ad2, ad3, ad4, ad5, ad6, ad7, ad8, ad9, ad10, ad11, ad12, ad13, ad14, ad15, c0, c1, c2,
       comparator_1_eq, comparator_2_eq, comparator_3_eq, op_or;
  wire [7:0] adder_1_out, adder_2_out, adder_3_out, adder_4_out, adder_5_out, adder_6_out, adder_7_out,
       adder_8_out, adder_9_out, adder_10_out, adder_11_out, adder_12_out, adder_13_out, adder_14_out,
       adder_15_out, adder_16_out, multiplexer_1_out, multiplier_1_cout, multiplier_1_out, multiplier_2_cout,
       multiplier_2_out, multiplier_3_cout, multiplier_3_out, multiplier_4_cout, multiplier_4_out,
       multiplier_5_cout, multiplier_5_out, multiplier_6_out, multiplier_7_out, multiplier_8_out,
       multiplier_9_cout, multiplier_9_out, multiplier_10_cout, multiplier_10_out, multiplier_11_cout,
       multiplier_11_out, multiplier_12_cout, multiplier_12_out, multiplier_13_out, multiplier_14_out,
       multiplier_15_out, multiplier_16_out, register_1_q;
  wire [23:0] multiplier_8_cout;
  wire [39:0] multiplier_15_cout;

  not not_1 (c2, comparator_1_eq);
  Comparator #(.width(16)) comparator_1 (
    .a({16{1'b0}}),
    .b({ad0, ad1, ad2, ad3, ad4, ad5, ad6, ad7, ad8, ad9, ad10, ad11, ad12, ad13, ad14, ad15}),
    .eq(comparator_1_eq));  // open: gt, lt
  Multiplier #(.mode("twosComplement")) multiplier_1 (
    .a(w0[7:0]), .b(x0[7:0]), .out(multiplier_1_out), .cout(multiplier_1_cout));  // open: cin
  Multiplier #(.mode("twosComplement")) multiplier_2 (
    .a(w0[15:8]), .b(x0[15:8]), .out(multiplier_2_out), .cout(multiplier_2_cout));  // open: cin
  Multiplier #(.mode("twosComplement")) multiplier_3 (
    .a(w0[23:16]), .b(x0[23:16]), .out(multiplier_3_out), .cout(multiplier_3_cout));  // open: cin
  Multiplier #(.mode("twosComplement")) multiplier_4 (
    .a(w0[31:24]), .b(x0[31:24]), .out(multiplier_4_out), .cout(multiplier_4_cout));  // open: cin
  Multiplier #(.mode("twosComplement")) multiplier_5 (
    .a(w0[39:32]), .b(x0[39:32]), .out(multiplier_5_out), .cout(multiplier_5_cout));  // open: cin
  Multiplier #(.mode("twosComplement")) multiplier_6 (
    .a(w0[47:40]), .b(x0[47:40]), .out(multiplier_6_out), .cout(multiplier_8_cout[23:16]));  // open: cin
  Multiplier #(.mode("twosComplement")) multiplier_7 (
    .a(w0[55:48]), .b(x0[55:48]), .out(multiplier_7_out), .cout(multiplier_8_cout[15:8]));  // open: cin
  Multiplier #(.mode("twosComplement")) multiplier_8 (
    .a(w0[63:56]), .b(x0[63:56]), .out(multiplier_8_out), .cout(multiplier_8_cout[7:0]));  // open: cin
  not not_2 (c0, comparator_2_eq);
  Comparator #(.width(64)) comparator_2 (
    .a({multiplier_1_cout, multiplier_2_cout, multiplier_3_cout, multiplier_4_cout, multiplier_5_cout, multiplier_8_cout}),
    .b({64{1'b0}}), .eq(comparator_2_eq));  // open: gt, lt
  or or_1 (op_or, c0, c1, c2);
  Adder adder_1 (.a(multiplier_1_out), .b(multiplier_2_out), .out(adder_1_out), .cout(ad0));  // open: cin
  Adder adder_2 (.a(multiplier_3_out), .b(multiplier_4_out), .out(adder_2_out), .cout(ad1));  // open: cin
  Adder adder_3 (.a(multiplier_5_out), .b(multiplier_6_out), .out(adder_3_out), .cout(ad2));  // open: cin
  Adder adder_4 (.a(multiplier_7_out), .b(multiplier_8_out), .out(adder_4_out), .cout(ad3));  // open: cin
  Adder adder_5 (.a(adder_1_out), .b(adder_2_out), .out(adder_5_out), .cout(ad4));  // open: cin
  Adder adder_6 (.a(adder_3_out), .b(adder_4_out), .out(adder_6_out), .cout(ad5));  // open: cin
  Adder adder_7 (.a(adder_5_out), .b(adder_6_out), .out(adder_7_out), .cout(ad6));  // open: cin
  Adder adder_8 (.a(adder_7_out), .b(adder_16_out), .out(adder_8_out), .cout(ad14));  // open: cin
  not not_3 (c1, comparator_3_eq);
  Comparator #(.width(64)) comparator_3 (
    .a({multiplier_9_cout, multiplier_10_cout, multiplier_11_cout, multiplier_15_cout[39:32], multiplier_12_cout, multiplier_15_cout[23:0]}),
    .b({64{1'b0}}), .eq(comparator_3_eq));  // open: gt, lt
  Multiplier #(.mode("twosComplement")) multiplier_9 (
    .a(w1[7:0]), .b(x1[7:0]), .out(multiplier_9_out), .cout(multiplier_9_cout));  // open: cin
  Multiplier #(.mode("twosComplement")) multiplier_10 (
    .a(w1[15:8]), .b(x1[15:8]), .out(multiplier_10_out), .cout(multiplier_10_cout));  // open: cin
  Multiplier #(.mode("twosComplement")) multiplier_11 (
    .a(w1[23:16]), .b(x1[23:16]), .out(multiplier_11_out), .cout(multiplier_11_cout));  // open: cin
  Multiplier #(.mode("twosComplement")) multiplier_12 (
    .a(w1[31:24]), .b(x1[31:24]), .out(multiplier_12_out), .cout(multiplier_12_cout));  // open: cin
  Multiplier #(.mode("twosComplement")) multiplier_13 (
    .a(w1[39:32]), .b(x1[39:32]), .out(multiplier_13_out), .cout(multiplier_15_cout[23:16]));  // open: cin
  Multiplier #(.mode("twosComplement")) multiplier_14 (
    .a(w1[47:40]), .b(x1[47:40]), .out(multiplier_14_out), .cout(multiplier_15_cout[15:8]));  // open: cin
  Multiplier #(.mode("twosComplement")) multiplier_15 (
    .a(w1[55:48]), .b(x1[55:48]), .out(multiplier_15_out), .cout(multiplier_15_cout[7:0]));  // open: cin
  Multiplier #(.mode("twosComplement")) multiplier_16 (
    .a(w1[63:56]), .b(x1[63:56]), .out(multiplier_16_out), .cout(multiplier_15_cout[39:32]));  // open: cin
  Adder adder_9 (.a(adder_8_out), .b(b), .out(adder_9_out), .cout(ad15));  // open: cin
  Adder adder_10 (.a(multiplier_9_out), .b(multiplier_10_out), .out(adder_10_out), .cout(ad7));  // open: cin
  Adder adder_11 (.a(multiplier_11_out), .b(multiplier_12_out), .out(adder_11_out), .cout(ad8));  // open: cin
  Adder adder_12 (.a(multiplier_13_out), .b(multiplier_14_out), .out(adder_12_out), .cout(ad9));  // open: cin
  Adder adder_13 (.a(multiplier_15_out), .b(multiplier_16_out), .out(adder_13_out), .cout(ad10));  // open: cin
  Multiplexer #(.width(8)) multiplexer_1 (.in0(adder_9_out), .in1({8{1'b1}}), .out(multiplexer_1_out), .sel(op_or));
  Adder adder_14 (.a(adder_10_out), .b(adder_11_out), .out(adder_14_out), .cout(ad11));  // open: cin
  Adder adder_15 (.a(adder_12_out), .b(adder_13_out), .out(adder_15_out), .cout(ad12));  // open: cin
  Adder adder_16 (.a(adder_14_out), .b(adder_15_out), .out(adder_16_out), .cout(ad13));  // open: cin
  Register #(.trigger("high")) register_1 (
    .D(multiplexer_1_out), .en(latch_ip), .clk(latch_ip), .Q(register_1_q), .clr(rst));
  Register register_2 (.D(register_1_q), .en(latch_op), .clk(latch_op), .Q(opt), .clr(rst));
  // Probe on opt
endmodule

module control_unit (
);

  wire clk, comparator_1_lt, comparator_4_eq, counter_1_q, is_l0, latch_op, multiplexer_2_out, not_1_out,
       rst, rst_l3, sel_bias;
  wire [1:0] layer;
  wire [2:0] rst_switch_sw3;
  wire [3:0] plex_index;
  wire [9:0] curr_iter;
  wire [15:0] multiplexer_1_out, rst_all;

  Comparator #(.mode("unsigned"), .width(10)) comparator_1 (
    .a(curr_iter), .b(10'h10), .lt(comparator_1_lt));  // open: gt, eq
  Multiplexer #(.select(3), .width(16)) multiplexer_1 (
    .in0({16{1'b0}}), .in1({16{1'b1}}), .in2(16'hf000), .out(multiplexer_1_out), .sel(rst_switch_sw3));  // open: in3, in4, in5, in6, in7
  DipSwitch #(.number(3)) rst_switch (.sw1(rst_switch_sw3[2]), .sw2(rst_switch_sw3[1]), .sw3(rst_switch_sw3[0]));
  Counter #(.max('h1), .width(1)) counter_1 (
    .Q(counter_1_q), .clk(comparator_4_eq), .clr(rst));  // open: load, D, count, carry, up
  and and_1 (sel_bias, is_l0, comparator_1_lt);
  Clock clock_1 (.out(clk));
  Button u_rst (.out(rst));
  Register #(.width(16)) register_1 (.D(multiplexer_1_out), .en(1'b1), .Q(rst_all), .clk(clk), .clr(rst));
  Button u_rst_l3 (.out(rst_l3));
  Counter #(.max('h3), .width(2)) counter_2 (
    .Q(layer), .clk(multiplexer_2_out), .clr(rst));  // open: load, D, count, carry, up
  Multiplexer multiplexer_2 (.in0(latch_op), .in1(comparator_4_eq), .out(multiplexer_2_out), .sel(not_1_out));
  not not_1 (not_1_out, counter_1_q);
  Counter #(.max('h3ff), .width(10)) counter_3 (
    .Q(curr_iter), .clk(clk), .clr(rst));  // open: load, D, count, carry, up
  Counter #(.max('hf), .width(4)) counter_4 (.Q(plex_index), .clk(clk), .clr(rst));  // open: load, D, count, carry, up
  Comparator #(.mode("unsigned"), .width(2)) comparator_2 (.a(layer), .b(2'b00), .eq(is_l0));  // open: gt, lt
  Comparator #(.mode("unsigned"), .width(4)) comparator_3 (.a(plex_index), .b(4'b1111), .eq(latch_op));  // open: gt, lt
  // Probe on layer
  Comparator #(.mode("unsigned"), .width(10)) comparator_4 (
    .a(curr_iter), .b({10{1'b1}}), .eq(comparator_4_eq));  // open: gt, lt

  // Other names for the same wires on the sheet: layer_done = latch_op
endmodule

module main (
);

  wire clk, comparator_1_eq, not_1_out, ram_en, rd_mem, rst;
  wire [2:0] sel_mac, sel_op;
  wire [4:0] rgb_video_1_p4, rgb_video_1_p5;
  wire [7:0] rom_img_data;
  wire [9:0] counter_1_q;
  wire [15:0] counter_2_q, ld_a_0, ld_a_1, ld_a_2, ld_a_3, ld_a_4, ld_a_5, ld_a_6, ld_a_7, ld_b_0, ld_b_1,
       ld_b_2, ld_b_3, ld_b_4, ld_b_5, ld_b_6, ld_b_7, op0, op1, op2, op3, op4, op5, op6, op7, w0, w1, w2,
       w3, w4, w5, w6, w7;
  wire [31:0] data_bus, ram_64k_32_dout, random_input_1_random_number;

  // Probe on ld_b_0
  // Probe on ld_a_0
  // Probe on ld_b_4
  // Probe on ld_a_4
  Multiplexer #(.select(3), .width(32)) multiplexer_1 (
    .in0({w0, op0}), .in1({w1, op1}), .in2({w2, op2}), .in3({w3, op3}), .in4({w4, op4}), .in5({w5, op5}),
    .in6({w6, op6}), .in7({w7, op7}), .out(data_bus), .sel(sel_op));
  mac mac_0 (.a(ld_a_0), .b(ld_b_0), .clk(clk), .rst(rst), .op(op0));
  mac mac_4 (.a(ld_a_4), .b(ld_b_4), .clk(clk), .rst(rst), .op(op4));
  // Probe on data_bus
  // Probe on op0
  // Probe on op4
  Demultiplexer #(.select(3), .width(32)) demultiplexer_1 (
    .out0({ld_a_0, ld_b_0}), .out1({ld_a_1, ld_b_1}), .out2({ld_a_2, ld_b_2}), .out3({ld_a_3, ld_b_3}),
    .out4({ld_a_4, ld_b_4}), .out5({ld_a_5, ld_b_5}), .out6({ld_a_6, ld_b_6}), .out7({ld_a_7, ld_b_7}),
    .in(data_bus), .sel(sel_mac));
  // Probe on sel_mac
  // Probe on ld_b_1
  // Probe on ld_b_5
  // Probe on ld_a_1
  // Probe on ld_a_5
  // Probe on op1
  mac mac_1 (.a(ld_a_1), .b(ld_b_1), .clk(clk), .rst(rst), .op(op1));
  // Probe on op5
  mac mac_5 (.a(ld_a_5), .b(ld_b_5), .clk(clk), .rst(rst), .op(op5));
  // Probe on ld_b_2
  // Probe on ld_b_6
  ROM #(.addrWidth(10)) rom_img (.addr(counter_1_q), .data(rom_img_data));
  // Probe on ld_a_2
  // Probe on ld_a_6
  Counter #(.max('h3ff), .width(10)) counter_1 (
    .Q(counter_1_q), .clk(clk), .clr(rst));  // open: load, D, count, carry, up
  // DipSwitch #(.number(2)) switch: pin names not known; wires that end beside it: rd_mem, ram_en, 1'b1
  Button u_rst (.out(rst));
  Clock clock_1 (.out(clk));
  // Probe on op2
  mac mac_2 (.a(ld_a_2), .b(ld_b_2), .clk(clk), .rst(rst), .op(op2));
  // Probe on op6
  mac mac_6 (.a(ld_a_6), .b(ld_b_6), .clk(clk), .rst(rst), .op(op6));
  random_input random_input_1 (.rst(rst), .clk(clk), .random_number(random_input_1_random_number));
  RAM #(.addrWidth(16), .dataWidth(32)) ram_64k_32 (
    .addr(counter_2_q), .we(not_1_out), .oe(rd_mem), .clk(clk), .din(random_input_1_random_number),
    .dout(ram_64k_32_dout));
  Counter #(.max('hffff), .width(16)) counter_2 (
    .load(1'b0), .D({16{1'b0}}), .count(1'b1), .Q(counter_2_q), .up(1'b1), .clk(clk), .clr(rst));  // open: carry
  not not_1 (not_1_out, rd_mem);
  // Probe on random_input_1_random_number
  // Probe on ld_b_3
  // Probe on ld_b_7
  // RGB_Video #(.height(32), .scale(8), .width(32)) rgb_video_1: pin names not known; wires that end beside it: rst, clk, 1'b1, rgb_video_1_p4, rgb_video_1_p5, {{16{1'b0}}, rom_img_data}
  Counter #(.max('h1f), .width(5)) x_cdnt (
    .Q(rgb_video_1_p4), .clk(clk), .clr(rst));  // open: load, D, count, carry, up
  // Probe on ld_a_3
  // Probe on ld_a_7
  Comparator #(.width(5)) comparator_1 (.a(rgb_video_1_p4), .b({5{1'b1}}), .eq(comparator_1_eq));  // open: gt, lt
  Counter #(.max('h1f), .width(5)) y_cdnt (
    .Q(rgb_video_1_p5), .clk(comparator_1_eq), .clr(rst));  // open: load, D, count, carry, up
  // Probe on ram_64k_32_dout[31:16]
  // Probe on ram_64k_32_dout[15:0]
  // Probe on op3
  mac mac_3 (.a(ld_a_3), .b(ld_b_3), .clk(clk), .rst(rst), .op(op3));
  // Probe on op7
  mac mac_7 (.a(ld_a_7), .b(ld_b_7), .clk(clk), .rst(rst), .op(op7));
  Counter #(.max('h7), .width(3)) counter_3 (.Q(sel_mac), .clk(clk));  // open: load, D, count, carry, up, clr
  assign data_bus = ram_en ? ram_64k_32_dout : 32'bz;  // Controlled_Buffer controlled_buffer_1

  // Notes on the sheet:
  //   contents of rom_img (hex, n*v repeats v):
  //   230*0 54 b9 9f 97 3c 24 26*0 de 4*fe f1 8*c6 aa 34 16*0 43 72 48 72 a3 e3 fe e1 fe fe fe fa e5 fe fe
  //   8c 21*0 11 42 e 43 43 43 3b 15 ec fe 6a 28*0 53 fd d1 12 27*0 16 e9 ff 53 28*0 81 fe ee 2c 27*0 3b
  //   f9 fe 3e 28*0 85 fe bb 5 27*0 9 cd f8 3a 28*0 7e fe b6 28*0 4b fb f0 39 27*0 13 dd fe a6 27*0 3 cb
  //   fe db 23 27*0 26 fe fe 4d 27*0 1f e0 fe 73 1 27*0 85 fe fe 34 27*0 3d f2 fe fe 34 27*0 79 fe fe db
  //   28 27*0 79 fe cf 12
endmodule

module mac (
  input  [15:0] a,
  input  [15:0] b,
  input  clk,
  input  rst,
  output [15:0] op
);

  wire not_1_out;
  wire [15:0] bit_extender_1_out, multiplexer_1_out, multiplexer_2_out, multiplier_1_out;

  assign bit_extender_1_out = {{15{1'b0}}, 1'b0};  // Bit_Extender bit_extender_1
  // Probe on a
  // Probe on b
  Multiplexer #(.width(16)) multiplexer_1 (.in0(bit_extender_1_out), .in1(a), .out(multiplexer_1_out), .sel(not_1_out));
  Multiplexer #(.width(16)) multiplexer_2 (.in0(bit_extender_1_out), .in1(b), .out(multiplexer_2_out), .sel(not_1_out));
  not not_1 (not_1_out, rst);
  // Probe on multiplier_1_out
  Multiplier #(.width(16)) multiplier_1 (
    .a(multiplexer_1_out), .b(multiplexer_2_out), .out(multiplier_1_out), .cin(op));  // open: cout
  // Probe on op
  Register #(.width(16)) register_1 (.D(multiplier_1_out), .en(1'b1), .clk(clk), .Q(op), .clr(rst));
endmodule

module random_input (
  input  rst,
  input  clk,
  output [31:0] random_number
);

  wire random_1_out;

  Random #(.width(1)) random_1 (.clk(clk), .out(random_1_out));  // open: clr, next
  Random random_2 (.clr(rst), .next(random_1_out), .clk(clk), .out(random_number[7:0]));
  Random random_3 (.clr(rst), .clk(clk), .out(random_number[23:16]));  // open: next
  // Probe on random_number[7:0]
  // Probe on random_number[23:16]
  // Probe on {{8{1'b0}}, random_number[7:0]}
  // Probe on {{8{1'b0}}, random_number[23:16]}
  // Probe on {{8{1'b0}}, random_number[23:16], {8{1'b0}}, random_number[7:0]}

  assign {random_number[31:24], random_number[15:8]} = {16{1'b0}};
endmodule

module dumping_ground (
  input  latch
);

  wire [7:0] register_1_q, undriven;

  Register register_1 (.D(undriven), .en(latch), .clk(latch), .Q(register_1_q));  // open: clr
endmodule

// VHDL entity softmax, as the project stores it:
--------------------------------------------------------------------------------
-- Project : mini-project
-- File    : softmax
-- Autor   : Hardik Ghoshal
-- Date    : 18/12/2022
--
--------------------------------------------------------------------------------
-- Description : A VHDL module which implements softmax function
--
--------------------------------------------------------------------------------


library IEEE;
use IEEE.NUMERIC_STD.ALL;

-- Softmax entity
entity softmax is
  port (
    x : in std_logic_vector(7 downto 0);
    y : out std_logic_vector(7 downto 0)
  );
end softmax;

-- Softmax architecture
architecture softmax_arch of softmax is
  variable result : std_logic_vector(7 downto 0);
  variable max_val : unsigned(7 downto 0);
  variable sum : unsigned(8 downto 0);
begin
  -- Normalize the input vector
  max_val := x(x'left);
  for i in x'range loop
    if x(i) > max_val then
      max_val := x(i);
    end if;
  end loop;
  for i in x'range loop
    result(i) := x(i) - max_val;
  end loop;
  
  -- Compute the exponential of each element in the normalized vector
  for i in x'range loop
    result(i) := unsigned(resize(exp(unsigned(result(i))), result(i)'range));
  end loop;
  
  -- Normalize the result vector
  sum := (others => '0');
  for i in x'range loop
    sum := sum + result(i);
  end loop;
  for i in x'range loop
    result(i) := result(i) * (255) / sum;
  end loop;
  
  -- Assign the result to the output
  y <= result;
end softmax_arch;

// VHDL entity ReLU, as the project stores it:
--------------------------------------------------------------------------------
-- Project : mini-project
-- File    : ReLU
-- Autor   : Hardik Ghoshal
-- Date    : 10/11/2022
--
--------------------------------------------------------------------------------
-- Description : A VHDL module which implements ReLU function
--
--------------------------------------------------------------------------------

library IEEE;
use IEEE.STD_LOGIC_1164.ALL;

entity ReLU is
    Port ( x : in  STD_LOGIC_VECTOR (7 downto 0);
           y : out  STD_LOGIC_VECTOR (7 downto 0));
end ReLU;

architecture Behavioral of ReLU is
begin
    y <= x when x >= "00000000" else "00000000";
end Behavioral;
