// Logisim project scratch.circ as structural Verilog: 1 circuit, main circuit main
module main (
  output [15:0] out_1
);

  wire clk, not_1_out;
  wire [15:0] counter_1_q, multiplier_1_out;

  Clock clock_1 (.out(clk));
  Adder #(.width(16)) adder_1 ();  // open: a, b, out, cin, cout
  Multiplier #(.width(16)) multiplier_1 (
    .a(16'h12), .b(16'h8f), .out(multiplier_1_out), .cin({16{1'b0}}));  // open: cout
  Multiplier #(.width(16)) multiplier_2 ();  // open: a, b, out, cin, cout
  Hex_Digit_Display hex_digit_display_1 (.value(multiplier_1_out[15:12]));  // open: dp
  Hex_Digit_Display hex_digit_display_2 (.value(multiplier_1_out[11:8]));  // open: dp
  Decoder decoder_1 ();  // open: out0, out1, sel, en
  Hex_Digit_Display hex_digit_display_3 (.value(multiplier_1_out[7:4]));  // open: dp
  Hex_Digit_Display hex_digit_display_4 (.value(multiplier_1_out[3:0]));  // open: dp
  Counter #(.max('hffff), .width(16)) counter_1 (
    .D(out_1), .Q(counter_1_q), .clk(clk));  // open: load, count, carry, up, clr
  RAM #(.addrWidth(16), .dataWidth(16)) ram_1 (
    .addr(counter_1_q), .we(1'b0), .oe(not_1_out), .clk(clk));  // open: din, dout
  not not_1 (not_1_out, 1'b0);

  // Other names for the same wires on the sheet: b_u_s[15:0] = out_1
endmodule
